// Logisim project projeto_graphics_cards.circ as structural Verilog: 3 circuits, main circuit Graphics_Card_256x128
module Graphics_Card_256x128 (
  input  R
);

  wire adder_1_cout, adder_2_cout, clock_1_out, or_1_out;
  wire [6:0] adder_2_out, bit_extender_2_out, rgb_video_1_p5;
  wire [7:0] adder_1_out, bit_extender_1_out, rgb_video_1_p4;
  wire [23:0] rgb_video_1_p6;

  Clock clock_1 (.out(clock_1_out));
  // RGB_Video #(.cursor("No Cursor"), .width(256)) rgb_video_1: pin names not known; wires that end beside it: R, clock_1_out, clock_1_out, rgb_video_1_p4, rgb_video_1_p5, rgb_video_1_p6
  Register register_1 (.D(adder_1_out), .en(clock_1_out), .clk(clock_1_out), .Q(rgb_video_1_p4), .clr(or_1_out));
  Register #(.width(7)) register_2 (
    .D(adder_2_out), .en(adder_1_cout), .clk(clock_1_out), .Q(rgb_video_1_p5), .clr(or_1_out));
  or or_1 (or_1_out, adder_2_cout, R);
  assign bit_extender_1_out = {{7{1'b0}}, 1'b1};  // Bit_Extender bit_extender_1
  assign bit_extender_2_out = {{6{1'b0}}, 1'b1};  // Bit_Extender bit_extender_2
  Adder adder_1 (.a(rgb_video_1_p4), .b(bit_extender_1_out), .out(adder_1_out), .cout(adder_1_cout));  // open: cin
  Adder #(.width(7)) adder_2 (
    .a(rgb_video_1_p5), .b(bit_extender_2_out), .out(adder_2_out), .cout(adder_2_cout));  // open: cin
  ROM #(.addrWidth(15), .dataWidth(24)) rom_1 (.addr({rgb_video_1_p5, rgb_video_1_p4}), .data(rgb_video_1_p6));

  // Notes on the sheet:
  //   contents of rom_1 (hex, n*v repeats v):
  //   828572 868975 898a76 8a8b77 888b77 878a77 858876 838575 7f8173 797d6f 72796b 6c7467 6a7168 697069
  //   6a706a 6b706a 676e68 666c66 696f69 737971 7d8076 878277 94826e af815c 9f7759 7a7160 596c6c 495957
  //   324037 2e3d36 2e3d35 2d3c36 2c3b36 2c3b38 2c3c39 2d3b3b 2b3a3b 293a3a 2a3a3b 2c3c3e 2c3d40 2f4043
  //   36454a 3e4c53 47535c 505962 575e66 5e656a 727574 89857e 959085 a09a8d a6a091 aca696 b4ae9f b8b2a6
  //   bfb8ae c5bcb6 cbc0bc d1c3c0 d4c6c3 d8c9c6 dacbc8 dbccc9 918f7a 91927c 94937e 93937d 91927d 8e917d
  //   8d907c 8a8d7a 858777 7f8173 7a7d6f 72796c 6e766b 6d746c 6d736c 6d736c 697169 616a63 5d6761 6d665b
  //   bd6644 ea6a21 f9790a f97c09 dc987b 81cfe7 61d8f6 76d9ec 609192 2e3e36 2d3b34 2b3b33 2b3a34 2c3a36
  //   2b3a37 2a3a37 293936 283837 263637 273738 29383b 293b3f 2c3d41 2f3f45 37464d 414d55 49555b 505a60
  //   63686c 787777 89867f 9b9489 a69f8e aba593 b2ac9d b9b3a6 c1bab0 c8bfb9 cec4c1 d3c6c4 d6c9c5 d9cbc7
  //   dacbc8 dbcbca 9f9d83 a09e85 a09f86 9f9d85 9b9b84 979883 949781 91947f 8d8e7c 878979 7f8373 777e6f
  //   747b6e 727a6f 70766f 6f746d 6a726b 636c64 8a6652 df6025 fb5f05 fa5b05 f64907 be688b 54c0ef 34c4f6
  //   41d0f8 64dbed 9cefce 9dbf76 5f6e3d 2b3932 2b3832 2a3833 293833 293736 283735 273734 253635 243635
  //   243636 26383a 27383e 27383e 2a3c42 32434a 3b4b50 445257 515c5f 62696b 777975 8c8a81 9c9889 a9a495
  //   b3ad9f b9b4a7 c2bab1 cac1bb cfc7c1 d2c8c6 d5cac8 d7cac7 d9cbc6 dacbc6 ada98e adaa8f adaa90 a8a58c
  //   a3a188 9f9f87 9b9d85 969882 919280 8b8d7c 858978 7d8373 797f71 757d71 737b71 70776e 6c736c 986f56
  //   f16715 f44d05 f33f05 e22b08 b22526 4ea0de 25b6f5 1caff1 41cfe4 75c966 9bd213 b3dd0e c9e12f a0b237
  //   455135 293832 283732 273633 263633 253532 253533 253534 233535 243638 24363c 24363b 26373e 2a3b42
  //   314347 38494f 415053 4f5a5c 656b69 7b7d78 96948a a8a597 b6b1a3 beb7ab c4bbb4 cbc2be d0c7c4 d3c9c7
  //   d5cbc9 d7ccc9 d8cbc5 d8cac2 b6b298 b5b196 b4af94 afac92 a8a68d a4a48a a1a187 9b9d85 959782 90927f
  //   8a8c7b 848778 7e8274 777f70 757e71 72796f 847165 eb591e e63a05 cd2907 c01d09 ad1c09 b13443 2e9fee
  //   16a1f1 1cbdf1 4fb08e 72b918 8fc105 9ebf05 b7ce06 c6d71c ced549 7a7f39 283730 273632 263633 253532
  //   243432 233432 223434 223436 243539 24363b 25363d 27383f 2b3d42 324348 37484c 425152 576263 737777
  //   91918a a8a59c b8b2aa c1bab3 c8c0bb cfc4c2 d2c9c8 d5ccca d5cbca d6cbc9 d5cac3 d5c9bf bdb79f bbb59a
  //   b9b498 b4b295 adac90 a9a78e a6a58b a2a188 9b9c85 959781 8f917e 898b7a 808577 798272 7e8579 b8bab2
  //   e9887b de2705 b82307 a7170c ae1206 b41808 862324 288bd8 12acf5 2cadd5 5fad4e 6da61a 85af0b 8caf04
  //   93ac07 a4b205 c0c606 cece16 8d9234 293831 253532 233431 223431 213432 213333 213436 223536 233638
  //   243739 24383b 273a3e 283c3f 2f4245 3a4b4e 505d61 6b7176 8b8c89 a8a59f bab3af c3bbb8 cac2bf d0c5c4
  //   d1c9c7 d3cbca d4cbcb d2cac7 d1c9bf cec6b8 c2bca4 c0bba1 bcb89b b7b597 b2b093 aead91 aba98e a5a58b
  //   a0a288 9a9c85 949782 8e917e 868b7b a5aa9f ebedea ebc8cc c32519 950d06 632d41 3d314d 652a39 a7190a
  //   901e1a 2a95dd 17a9f3 3ca5ab 5fa046 74a719 739f15 739514 88a00c 95aa09 9caf06 b3be05 c6ca2d a5a843
  //   2a3a31 233532 213431 203331 213333 1f3433 1f3435 203536 223738 233738 24373d 24393e 2b3f41 37484c
  //   4c5a60 666f75 888a8b a8a49f bab2b2 c3baba cac1bf cfc5c4 d1c8c6 d2cac8 d2cac7 cfc7c1 cbc5b8 c5bfaf
  //   c8c2aa c5bfa6 c1bca0 bcb89b b7b396 b4b094 b1ae91 aaa98e a5a48b a0a089 999b87 959787 c3c5bc f9faf8
  //   f4f3fa c38b9e 9b1105 81120e 39263b 9091a 473859 96190f 8a1923 339de8 23b9f2 42adab 61a549 659735
  //   658e2f 678327 81a00d 84a409 81980b 94a408 a5b30d b3bb2f 8c933d 243631 203331 203331 223232 203232
  //   1f3334 1f3435 203536 203537 22373c 23363c 283c40 36484d 4a595f 626b75 81868a a19f9e b6afb0 bfb7b7
  //   c7bfbf cdc4c5 d2c8c7 d4c9c8 d1c7c5 cac4ba c3bdad bab5a1 cbc5af c8c2aa c4bea5 c0bb9f bab69a b7b397
  //   b1af95 adab91 a9a78e a5a58d a3a28e d7d6cf faf4f6 f6e6ea e6c3c5 c48787 891e0b 7b160b 59364d 473657
  //   963453 a20905 a1120e 4891cb 24adeb 45afb2 5ea152 659731 608b25 577923 607f1f 698b15 779817 839b1c
  //   8da123 9bab27 b0b647 797f46 213331 203330 1f3131 1e3232 1e3334 1e3334 1f3435 1f3535 203638 223639
  //   263c3f 32474c 45565e 616a75 7a8188 939496 aba6a6 b7b1b1 c0baba c8c0c1 cec5c4 d2c8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
endmodule

module Graphics_Card_128x64 (
  input  R
);

  wire adder_1_cout, adder_2_cout, clock_1_out, or_1_out;
  wire [5:0] adder_2_out, bit_extender_2_out, rgb_video_1_p5;
  wire [6:0] adder_1_out, bit_extender_1_out, rgb_video_1_p4;
  wire [23:0] rgb_video_1_p6;

  Clock clock_1 (.out(clock_1_out));
  // RGB_Video #(.cursor("No Cursor"), .height(64), .scale(4)) rgb_video_1: pin names not known; wires that end beside it: R, clock_1_out, clock_1_out, rgb_video_1_p4, rgb_video_1_p5, rgb_video_1_p6
  Register #(.width(7)) register_1 (
    .D(adder_1_out), .en(clock_1_out), .clk(clock_1_out), .Q(rgb_video_1_p4), .clr(or_1_out));
  Register #(.width(6)) register_2 (
    .D(adder_2_out), .en(adder_1_cout), .clk(clock_1_out), .Q(rgb_video_1_p5), .clr(or_1_out));
  or or_1 (or_1_out, adder_2_cout, R);
  assign bit_extender_1_out = {{6{1'b0}}, 1'b1};  // Bit_Extender bit_extender_1
  assign bit_extender_2_out = {{5{1'b0}}, 1'b1};  // Bit_Extender bit_extender_2
  Adder #(.width(7)) adder_1 (
    .a(rgb_video_1_p4), .b(bit_extender_1_out), .out(adder_1_out), .cout(adder_1_cout));  // open: cin
  Adder #(.width(6)) adder_2 (
    .a(rgb_video_1_p5), .b(bit_extender_2_out), .out(adder_2_out), .cout(adder_2_cout));  // open: cin
  ROM #(.addrWidth(13), .dataWidth(24)) rom_1 (.addr({rgb_video_1_p5, rgb_video_1_p4}), .data(rgb_video_1_p6));

  // Notes on the sheet:
  //   contents of rom_1 (hex, n*v repeats v):
  //   828572 868975 898a76 8a8b77 888b77 878a77 858876 838575 7f8173 797d6f 72796b 6c7467 6a7168 697069
  //   6a706a 6b706a 676e68 666c66 696f69 737971 7d8076 878277 94826e af815c 9f7759 7a7160 596c6c 495957
  //   324037 2e3d36 2e3d35 2d3c36 2c3b36 2c3b38 2c3c39 2d3b3b 2b3a3b 293a3a 2a3a3b 2c3c3e 2c3d40 2f4043
  //   36454a 3e4c53 47535c 505962 575e66 5e656a 727574 89857e 959085 a09a8d a6a091 aca696 b4ae9f b8b2a6
  //   bfb8ae c5bcb6 cbc0bc d1c3c0 d4c6c3 d8c9c6 dacbc8 dbccc9 918f7a 91927c 94937e 93937d 91927d 8e917d
  //   8d907c 8a8d7a 858777 7f8173 7a7d6f 72796c 6e766b 6d746c 6d736c 6d736c 697169 616a63 5d6761 6d665b
  //   bd6644 ea6a21 f9790a f97c09 dc987b 81cfe7 61d8f6 76d9ec 609192 2e3e36 2d3b34 2b3b33 2b3a34 2c3a36
  //   2b3a37 2a3a37 293936 283837 263637 273738 29383b 293b3f 2c3d41 2f3f45 37464d 414d55 49555b 505a60
  //   63686c 787777 89867f 9b9489 a69f8e aba593 b2ac9d b9b3a6 c1bab0 c8bfb9 cec4c1 d3c6c4 d6c9c5 d9cbc7
  //   dacbc8 dbcbca 9f9d83 a09e85 a09f86 9f9d85 9b9b84 979883 949781 91947f 8d8e7c 878979 7f8373 777e6f
  //   747b6e 727a6f 70766f 6f746d 6a726b 636c64 8a6652 df6025 fb5f05 fa5b05 f64907 be688b 54c0ef 34c4f6
  //   41d0f8 64dbed 9cefce 9dbf76 5f6e3d 2b3932 2b3832 2a3833 293833 293736 283735 273734 253635 243635
  //   243636 26383a 27383e 27383e 2a3c42 32434a 3b4b50 445257 515c5f 62696b 777975 8c8a81 9c9889 a9a495
  //   b3ad9f b9b4a7 c2bab1 cac1bb cfc7c1 d2c8c6 d5cac8 d7cac7 d9cbc6 dacbc6 ada98e adaa8f adaa90 a8a58c
  //   a3a188 9f9f87 9b9d85 969882 919280 8b8d7c 858978 7d8373 797f71 757d71 737b71 70776e 6c736c 986f56
  //   f16715 f44d05 f33f05 e22b08 b22526 4ea0de 25b6f5 1caff1 41cfe4 75c966 9bd213 b3dd0e c9e12f a0b237
  //   455135 293832 283732 273633 263633 253532 253533 253534 233535 243638 24363c 24363b 26373e 2a3b42
  //   314347 38494f 415053 4f5a5c 656b69 7b7d78 96948a a8a597 b6b1a3 beb7ab c4bbb4 cbc2be d0c7c4 d3c9c7
  //   d5cbc9 d7ccc9 d8cbc5 d8cac2 b6b298 b5b196 b4af94 afac92 a8a68d a4a48a a1a187 9b9d85 959782 90927f
  //   8a8c7b 848778 7e8274 777f70 757e71 72796f 847165 eb591e e63a05 cd2907 c01d09 ad1c09 b13443 2e9fee
  //   16a1f1 1cbdf1 4fb08e 72b918 8fc105 9ebf05 b7ce06 c6d71c ced549 7a7f39 283730 273632 263633 253532
  //   243432 233432 223434 223436 243539 24363b 25363d 27383f 2b3d42 324348 37484c 425152 576263 737777
  //   91918a a8a59c b8b2aa c1bab3 c8c0bb cfc4c2 d2c9c8 d5ccca d5cbca d6cbc9 d5cac3 d5c9bf bdb79f bbb59a
  //   b9b498 b4b295 adac90 a9a78e a6a58b a2a188 9b9c85 959781 8f917e 898b7a 808577 798272 7e8579 b8bab2
  //   e9887b de2705 b82307 a7170c ae1206 b41808 862324 288bd8 12acf5 2cadd5 5fad4e 6da61a 85af0b 8caf04
  //   93ac07 a4b205 c0c606 cece16 8d9234 293831 253532 233431 223431 213432 213333 213436 223536 233638
  //   243739 24383b 273a3e 283c3f 2f4245 3a4b4e 505d61 6b7176 8b8c89 a8a59f bab3af c3bbb8 cac2bf d0c5c4
  //   d1c9c7 d3cbca d4cbcb d2cac7 d1c9bf cec6b8 c2bca4 c0bba1 bcb89b b7b597 b2b093 aead91 aba98e a5a58b
  //   a0a288 9a9c85 949782 8e917e 868b7b a5aa9f ebedea ebc8cc c32519 950d06 632d41 3d314d 652a39 a7190a
  //   901e1a 2a95dd 17a9f3 3ca5ab 5fa046 74a719 739f15 739514 88a00c 95aa09 9caf06 b3be05 c6ca2d a5a843
  //   2a3a31 233532 213431 203331 213333 1f3433 1f3435 203536 223738 233738 24373d 24393e 2b3f41 37484c
  //   4c5a60 666f75 888a8b a8a49f bab2b2 c3baba cac1bf cfc5c4 d1c8c6 d2cac8 d2cac7 cfc7c1 cbc5b8 c5bfaf
  //   c8c2aa c5bfa6 c1bca0 bcb89b b7b396 b4b094 b1ae91 aaa98e a5a48b a0a089 999b87 959787 c3c5bc f9faf8
  //   f4f3fa c38b9e 9b1105 81120e 39263b 9091a 473859 96190f 8a1923 339de8 23b9f2 42adab 61a549 659735
  //   658e2f 678327 81a00d 84a409 81980b 94a408 a5b30d b3bb2f 8c933d 243631 203331 203331 223232 203232
  //   1f3334 1f3435 203536 203537 22373c 23363c 283c40 36484d 4a595f 626b75 81868a a19f9e b6afb0 bfb7b7
  //   c7bfbf cdc4c5 d2c8c7 d4c9c8 d1c7c5 cac4ba c3bdad bab5a1 cbc5af c8c2aa c4bea5 c0bb9f bab69a b7b397
  //   b1af95 adab91 a9a78e a5a58d a3a28e d7d6cf faf4f6 f6e6ea e6c3c5 c48787 891e0b 7b160b 59364d 473657
  //   963453 a20905 a1120e 4891cb 24adeb 45afb2 5ea152 659731 608b25 577923 607f1f 698b15 779817 839b1c
  //   8da123 9bab27 b0b647 797f46 213331 203330 1f3131 1e3232 1e3334 1e3334 1f3435 1f3535 203638 223639
  //   263c3f 32474c 45565e 616a75 7a8188 939496 aba6a6 b7b1b1 c0baba c8c0c1 cec5c4 d2c8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
endmodule

module Graphics_Card_64x32 (
  input  R
);

  wire adder_1_cout, adder_2_cout, clock_1_out, or_1_out;
  wire [4:0] adder_2_out, bit_extender_2_out, rgb_video_1_p5;
  wire [5:0] adder_1_out, bit_extender_1_out, rgb_video_1_p4;
  wire [23:0] rgb_video_1_p6;

  Clock clock_1 (.out(clock_1_out));
  // RGB_Video #(.cursor("No Cursor"), .height(32), .scale(5), .width(64)) rgb_video_1: pin names not known; wires that end beside it: R, clock_1_out, clock_1_out, rgb_video_1_p4, rgb_video_1_p5, rgb_video_1_p6
  Register #(.width(6)) register_1 (
    .D(adder_1_out), .en(clock_1_out), .clk(clock_1_out), .Q(rgb_video_1_p4), .clr(or_1_out));
  Register #(.width(5)) register_2 (
    .D(adder_2_out), .en(adder_1_cout), .clk(clock_1_out), .Q(rgb_video_1_p5), .clr(or_1_out));
  or or_1 (or_1_out, adder_2_cout, R);
  assign bit_extender_1_out = {{5{1'b0}}, 1'b1};  // Bit_Extender bit_extender_1
  assign bit_extender_2_out = {{4{1'b0}}, 1'b1};  // Bit_Extender bit_extender_2
  Adder #(.width(6)) adder_1 (
    .a(rgb_video_1_p4), .b(bit_extender_1_out), .out(adder_1_out), .cout(adder_1_cout));  // open: cin
  Adder #(.width(5)) adder_2 (
    .a(rgb_video_1_p5), .b(bit_extender_2_out), .out(adder_2_out), .cout(adder_2_cout));  // open: cin
  ROM #(.addrWidth(11), .dataWidth(24)) rom_1 (.addr({rgb_video_1_p5, rgb_video_1_p4}), .data(rgb_video_1_p6));

  // Notes on the sheet:
  //   contents of rom_1 (hex, n*v repeats v):
  //   828572 868975 898a76 8a8b77 888b77 878a77 858876 838575 7f8173 797d6f 72796b 6c7467 6a7168 697069
  //   6a706a 6b706a 676e68 666c66 696f69 737971 7d8076 878277 94826e af815c 9f7759 7a7160 596c6c 495957
  //   324037 2e3d36 2e3d35 2d3c36 2c3b36 2c3b38 2c3c39 2d3b3b 2b3a3b 293a3a 2a3a3b 2c3c3e 2c3d40 2f4043
  //   36454a 3e4c53 47535c 505962 575e66 5e656a 727574 89857e 959085 a09a8d a6a091 aca696 b4ae9f b8b2a6
  //   bfb8ae c5bcb6 cbc0bc d1c3c0 d4c6c3 d8c9c6 dacbc8 dbccc9 918f7a 91927c 94937e 93937d 91927d 8e917d
  //   8d907c 8a8d7a 858777 7f8173 7a7d6f 72796c 6e766b 6d746c 6d736c 6d736c 697169 616a63 5d6761 6d665b
  //   bd6644 ea6a21 f9790a f97c09 dc987b 81cfe7 61d8f6 76d9ec 609192 2e3e36 2d3b34 2b3b33 2b3a34 2c3a36
  //   2b3a37 2a3a37 293936 283837 263637 273738 29383b 293b3f 2c3d41 2f3f45 37464d 414d55 49555b 505a60
  //   63686c 787777 89867f 9b9489 a69f8e aba593 b2ac9d b9b3a6 c1bab0 c8bfb9 cec4c1 d3c6c4 d6c9c5 d9cbc7
  //   dacbc8 dbcbca 9f9d83 a09e85 a09f86 9f9d85 9b9b84 979883 949781 91947f 8d8e7c 878979 7f8373 777e6f
  //   747b6e 727a6f 70766f 6f746d 6a726b 636c64 8a6652 df6025 fb5f05 fa5b05 f64907 be688b 54c0ef 34c4f6
  //   41d0f8 64dbed 9cefce 9dbf76 5f6e3d 2b3932 2b3832 2a3833 293833 293736 283735 273734 253635 243635
  //   243636 26383a 27383e 27383e 2a3c42 32434a 3b4b50 445257 515c5f 62696b 777975 8c8a81 9c9889 a9a495
  //   b3ad9f b9b4a7 c2bab1 cac1bb cfc7c1 d2c8c6 d5cac8 d7cac7 d9cbc6 dacbc6 ada98e adaa8f adaa90 a8a58c
  //   a3a188 9f9f87 9b9d85 969882 919280 8b8d7c 858978 7d8373 797f71 757d71 737b71 70776e 6c736c 986f56
  //   f16715 f44d05 f33f05 e22b08 b22526 4ea0de 25b6f5 1caff1 41cfe4 75c966 9bd213 b3dd0e c9e12f a0b237
  //   455135 293832 283732 273633 263633 253532 253533 253534 233535 243638 24363c 24363b 26373e 2a3b42
  //   314347 38494f 415053 4f5a5c 656b69 7b7d78 96948a a8a597 b6b1a3 beb7ab c4bbb4 cbc2be d0c7c4 d3c9c7
  //   d5cbc9 d7ccc9 d8cbc5 d8cac2 b6b298 b5b196 b4af94 afac92 a8a68d a4a48a a1a187 9b9d85 959782 90927f
  //   8a8c7b 848778 7e8274 777f70 757e71 72796f 847165 eb591e e63a05 cd2907 c01d09 ad1c09 b13443 2e9fee
  //   16a1f1 1cbdf1 4fb08e 72b918 8fc105 9ebf05 b7ce06 c6d71c ced549 7a7f39 283730 273632 263633 253532
  //   243432 233432 223434 223436 243539 24363b 25363d 27383f 2b3d42 324348 37484c 425152 576263 737777
  //   91918a a8a59c b8b2aa c1bab3 c8c0bb cfc4c2 d2c9c8 d5ccca d5cbca d6cbc9 d5cac3 d5c9bf bdb79f bbb59a
  //   b9b498 b4b295 adac90 a9a78e a6a58b a2a188 9b9c85 959781 8f917e 898b7a 808577 798272 7e8579 b8bab2
  //   e9887b de2705 b82307 a7170c ae1206 b41808 862324 288bd8 12acf5 2cadd5 5fad4e 6da61a 85af0b 8caf04
  //   93ac07 a4b205 c0c606 cece16 8d9234 293831 253532 233431 223431 213432 213333 213436 223536 233638
  //   243739 24383b 273a3e 283c3f 2f4245 3a4b4e 505d61 6b7176 8b8c89 a8a59f bab3af c3bbb8 cac2bf d0c5c4
  //   d1c9c7 d3cbca d4cbcb d2cac7 d1c9bf cec6b8 c2bca4 c0bba1 bcb89b b7b597 b2b093 aead91 aba98e a5a58b
  //   a0a288 9a9c85 949782 8e917e 868b7b a5aa9f ebedea ebc8cc c32519 950d06 632d41 3d314d 652a39 a7190a
  //   901e1a 2a95dd 17a9f3 3ca5ab 5fa046 74a719 739f15 739514 88a00c 95aa09 9caf06 b3be05 c6ca2d a5a843
  //   2a3a31 233532 213431 203331 213333 1f3433 1f3435 203536 223738 233738 24373d 24393e 2b3f41 37484c
  //   4c5a60 666f75 888a8b a8a49f bab2b2 c3baba cac1bf cfc5c4 d1c8c6 d2cac8 d2cac7 cfc7c1 cbc5b8 c5bfaf
  //   c8c2aa c5bfa6 c1bca0 bcb89b b7b396 b4b094 b1ae91 aaa98e a5a48b a0a089 999b87 959787 c3c5bc f9faf8
  //   f4f3fa c38b9e 9b1105 81120e 39263b 9091a 473859 96190f 8a1923 339de8 23b9f2 42adab 61a549 659735
  //   658e2f 678327 81a00d 84a409 81980b 94a408 a5b30d b3bb2f 8c933d 243631 203331 203331 223232 203232
  //   1f3334 1f3435 203536 203537 22373c 23363c 283c40 36484d 4a595f 626b75 81868a a19f9e b6afb0 bfb7b7
  //   c7bfbf cdc4c5 d2c8c7 d4c9c8 d1c7c5 cac4ba c3bdad bab5a1 cbc5af c8c2aa c4bea5 c0bb9f bab69a b7b397
  //   b1af95 adab91 a9a78e a5a58d a3a28e d7d6cf faf4f6 f6e6ea e6c3c5 c48787 891e0b 7b160b 59364d 473657
  //   963453 a20905 a1120e 4891cb 24adeb 45afb2 5ea152 659731 608b25 577923 607f1f 698b15 779817 839b1c
  //   8da123 9bab27 b0b647 797f46 213331 203330 1f3131 1e3232 1e3334 1e3334 1f3435 1f3535 203638 223639
  //   263c3f 32474c 45565e 616a75 7a8188 939496 aba6a6 b7b1b1 c0baba c8c0c1 cec5c4 d2c8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
endmodule
